// Logisim project MUL.circ as structural Verilog: 1 circuit, main circuit main
module main (
  input  A0,
  input  A1,
  input  A2,
  input  A3,
  input  B0,
  input  B1,
  input  B2,
  input  B3,
  output R0,
  output R1,
  output R2,
  output R3,
  output R4,
  output R5,
  output R6,
  output R7
);

  wire [5:0] adder_1_out, and_1_out, and_2_out;
  wire [7:0] adder_2_out, and_3_out, and_4_out;

  assign and_1_out = {2'b00, A3, A2, A1, A0} & {6{B0}};  // AND_Gate and_1, 6 bits wide
  assign and_2_out = {1'b0, A3, A2, A1, A0, 1'b0} & {6{B1}};  // AND_Gate and_2, 6 bits wide
  assign and_3_out = {2'b00, A3, A2, A1, A0, 2'b00} & {8{B2}};  // AND_Gate and_3, 8 bits wide
  assign and_4_out = {1'b0, A3, A2, A1, A0, 3'b000} & {8{B3}};  // AND_Gate and_4, 8 bits wide
  Adder #(.width(6)) adder_1 (.a(and_1_out), .b(and_2_out), .out(adder_1_out));  // open: cin, cout
  Adder adder_2 (.a({2'b00, adder_1_out}), .b(and_3_out), .out(adder_2_out));  // open: cin, cout
  Adder adder_3 (.a(adder_2_out), .b(and_4_out), .out({R7, R6, R5, R4, R3, R2, R1, R0}));  // open: cin, cout
endmodule
